// Logisim project Oscillation.circ as structural Verilog: 1 circuit, main circuit main
module main (
  input  in_1,
  output out_2
);

  wire not_1_out;

  or or_1 (out_2, in_1, not_1_out);
  not not_1 (not_1_out, out_2);
endmodule
