// Logisim project synchronization issue.circ as structural Verilog: 1 circuit, main circuit main
module main (
  input  in_1,
  output out_2
);

  wire not_1_out;

  not not_1 (not_1_out, in_1);
  and and_1 (out_2, in_1, not_1_out);
endmodule
